# Fritzing sketch module3 (saved by Fritzing 0.9.3b)
breadboards: 1

parts:
  R3 = Resistor [tolerance=±5% resistance=10k package="1206 [SMD]"]
  Gizwits_WiFi_Witty_ESP-12F1 = Gizwits WiFi Witty ESP-12F  # not connected
  R2 = Resistor [tolerance=±5% resistance=10k package="1206 [SMD]"]
  J1 = Camdenboss CTB0158-7 [part_number=CTB0158-7 package=THT]
  IRLB8723 = npn-Powertransistor [package="TO220 [THT]"]
  IRLB8722 = npn-Powertransistor [package="TO220 [THT]"]
  R4 = Resistor [tolerance=±5% resistance=10k package="1206 [SMD]"]
  IRLB8724 = npn-Powertransistor [package="TO220 [THT]"]
  LM1 = RioRand LM2596  # not connected

nets:
  N1: R3.Pin_0, R2.Pin_0, R4.Pin_0
  N2: R3.Pin_1, R2.Pin_1, IRLB8723.base, IRLB8722.base, R4.Pin_1, IRLB8724.base
  N3: J1.pin1, IRLB8724.collector
  N4: J1.pin2, IRLB8722.collector
  N5: J1.pin3, IRLB8723.collector
  N6: J1.pin7, IRLB8723.emitter, IRLB8722.emitter, IRLB8724.emitter
